// Logisim project control_logic.circ as structural Verilog: 1 circuit, main circuit control_logic
module control_logic (
  input  [31:0] inst,
  input  BrEq,
  input  BrLt,
  output PCSel,
  output RegWEn,
  output [2:0] ImmSel,
  output BrUn,
  output ASel,
  output BSel,
  output [3:0] ALUSel,
  output MemRW,
  output [1:0] WBSel,
  output CSRSel,
  output CSRWen
);

  wire auipc, comparator_11_eq, decoder_1_out0, decoder_1_out1, decoder_1_out2, decoder_1_out3,
       decoder_1_out4, decoder_1_out5, decoder_1_out6, decoder_1_out7, demultiplexer_1_out0,
       demultiplexer_1_out1, demultiplexer_1_out2, demultiplexer_2_out0, demultiplexer_2_out1,
       demultiplexer_3_out0, demultiplexer_3_out2, I, jal, jalr, load, lui, or_5_out, or_6_out, R, SB, store;
  wire [1:0] funct7Sel, or_1_out, or_9_out;
  wire [3:0] controlled_buffer_1_out;
  wire [6:2] undriven;

  Comparator #(.width(7)) comparator_1 (.a(inst[6:0]), .b(7'b0110011), .eq(R));  // open: gt, lt
  Comparator #(.width(7)) comparator_2 (.a(inst[6:0]), .b(7'b0000011), .eq(load));  // open: gt, lt
  Comparator #(.width(7)) comparator_3 (.a(inst[6:0]), .b(7'b0010011), .eq(I));  // open: gt, lt
  Comparator #(.width(7)) comparator_4 (.a(inst[6:0]), .b(7'b0100011), .eq(store));  // open: gt, lt
  Comparator #(.width(7)) comparator_5 (.a(inst[6:0]), .b(7'b1100011), .eq(SB));  // open: gt, lt
  Comparator #(.width(7)) comparator_6 (.a(inst[6:0]), .b(7'b0010111), .eq(auipc));  // open: gt, lt
  Comparator #(.width(7)) comparator_7 (.a(inst[6:0]), .b(7'b0110111), .eq(lui));  // open: gt, lt
  Comparator #(.width(7)) comparator_8 (.a(inst[6:0]), .b(7'b1101111), .eq(jal));  // open: gt, lt
  Comparator #(.width(7)) comparator_9 (.a(inst[6:0]), .b(7'b1100111), .eq(jalr));  // open: gt, lt
  Comparator #(.width(7)) comparator_10 (.a(inst[6:0]), .b(7'b1110011), .eq(CSRWen));  // open: gt, lt
  // NOR_Gate nor_1 has open pins: in0=SB, in1=jal, in2=jalr, out=open
  or or_1 (or_1_out[0], store, auipc, lui);
  or or_2 (or_1_out[1], SB, auipc, lui);
  // OR_Gate or_3 has open pins: in0=SB, in1=auipc, in2=jal, out=open
  // OR_Gate or_4 has open pins: in0=load, in1=I, in2=auipc, in3=lui, in4=jal, in5=jalr, in6=CSRWen, out=open
  Bit_Extender #(.in_width(7), .out_width(2)) bit_extender_1 (.in({undriven, inst[30], inst[25]}), .out(funct7Sel));
  Decoder #(.select(3)) decoder_1 (
    .out0(decoder_1_out0), .out1(decoder_1_out1), .out2(decoder_1_out2), .out3(decoder_1_out3),
    .out4(decoder_1_out4), .out5(decoder_1_out5), .out6(decoder_1_out6), .out7(decoder_1_out7),
    .sel(inst[14:12]), .en(or_5_out));
  or or_5 (or_5_out, R, I);
  or or_6 (or_6_out, load, store, SB, jal, jalr, auipc);
  // OR_Gate or_7 has open pins: in0=load, in1=store, out=open
  Comparator #(.width(3)) comparator_11 (.a(inst[14:12]), .b(3'b101), .eq(comparator_11_eq));  // open: gt, lt
  // OR_Gate or_8 has open pins: in0=R, in1=load, in2=I, in3=auipc, in4=lui, in5=jal, in6=jalr, out=open
  // AND_Gate and_1 has open pins: in0=SB, in1=inst[13], out=open
  or or_9 (or_9_out[0], store, CSRWen);
  or or_10 (or_9_out[1], SB, jal, jalr, CSRWen);
  and and_2 (CSRSel, CSRWen, comparator_11_eq);
  Demultiplexer #(.enable("false"), .select(2)) demultiplexer_1 (
    .out0(demultiplexer_1_out0), .out1(demultiplexer_1_out1), .out2(demultiplexer_1_out2),
    .in(decoder_1_out0), .sel(funct7Sel));  // open: out3
  Demultiplexer #(.enable("false"), .select(2)) demultiplexer_2 (
    .out0(demultiplexer_2_out0), .out1(demultiplexer_2_out1), .in(decoder_1_out1), .sel(funct7Sel));  // open: out2, out3
  assign controlled_buffer_1_out = decoder_1_out2 ? 4'b0111 : 4'bz;  // Controlled_Buffer controlled_buffer_1
  assign controlled_buffer_1_out = decoder_1_out3 ? 4'b1011 : 4'bz;  // Controlled_Buffer controlled_buffer_2
  assign controlled_buffer_1_out = decoder_1_out4 ? 4'b0011 : 4'bz;  // Controlled_Buffer controlled_buffer_3
  Demultiplexer #(.enable("false"), .select(2)) demultiplexer_3 (
    .out0(demultiplexer_3_out0), .out2(demultiplexer_3_out2), .in(decoder_1_out5), .sel(funct7Sel));  // open: out1, out3
  assign controlled_buffer_1_out = decoder_1_out6 ? 4'b0010 : 4'bz;  // Controlled_Buffer controlled_buffer_4
  assign controlled_buffer_1_out = decoder_1_out7 ? 4'b0001 : 4'bz;  // Controlled_Buffer controlled_buffer_5
  assign controlled_buffer_1_out = or_6_out ? 4'b0000 : 4'bz;  // Controlled_Buffer controlled_buffer_6
  assign controlled_buffer_1_out = lui ? 4'b1101 : 4'bz;  // Controlled_Buffer controlled_buffer_7
  assign controlled_buffer_1_out = CSRWen ? 4'b1000 : 4'bz;  // Controlled_Buffer controlled_buffer_8
  assign controlled_buffer_1_out = demultiplexer_1_out0 ? 4'b0000 : 4'bz;  // Controlled_Buffer controlled_buffer_9
  assign controlled_buffer_1_out = demultiplexer_1_out1 ? 4'b1010 : 4'bz;  // Controlled_Buffer controlled_buffer_10
  assign controlled_buffer_1_out = demultiplexer_2_out0 ? 4'b0110 : 4'bz;  // Controlled_Buffer controlled_buffer_11
  assign controlled_buffer_1_out = demultiplexer_2_out1 ? 4'b1110 : 4'bz;  // Controlled_Buffer controlled_buffer_12
  assign controlled_buffer_1_out = demultiplexer_3_out0 ? 4'b0100 : 4'bz;  // Controlled_Buffer controlled_buffer_13
  assign controlled_buffer_1_out = demultiplexer_1_out2 ? 4'b1100 : 4'bz;  // Controlled_Buffer controlled_buffer_14
  assign controlled_buffer_1_out = demultiplexer_3_out2 ? 4'b0101 : 4'bz;  // Controlled_Buffer controlled_buffer_15

  assign ALUSel = 4'b0000;
  assign ASel = 1'b0;
  assign BSel = 1'b1;
  assign ImmSel = 3'b000;
  assign MemRW = 1'b0;
  assign PCSel = 1'b1;
  assign RegWEn = 1'b1;
  assign WBSel = 2'b00;

  // Other names for the same wires on the sheet: funct7[6:0] = inst[31:25]; csr = CSRWen; opcode[6:0] = inst[6:0];
  //   funct3[2:0] = inst[14:12]

  // Notes on the sheet:
  //   INPUTS to your circuit
  //   DON'T CHANGE THE LOCATIONS OF THE INPUTS AND OUTPUTS!
  //   OUTPUT from your circuit
  //   I
  //   SB
  //   lui
  //   jal
  //   R
  //   I
  //   S
  //   auipc
  //   jalr
  //   csrw, csrwi
  //   the significant bit is bit1
endmodule
