// Logisim project cpu.circ as structural Verilog: 1 circuit, main circuit cpu
module cpu (
  input  clk,
  input  [31:0] INSTRUCTION,
  input  [31:0] READ_DATA,
  output [31:0] WRITE_ADDRESS,
  output [31:0] PROGRAM_COUNTER,
  output [31:0] ra,
  output [31:0] sp,
  output [31:0] t0,
  output [31:0] t1,
  output [31:0] t2,
  output [31:0] s0,
  output [31:0] s1,
  output [31:0] a0,
  output [31:0] tohost,
  output [3:0] WRITE_ENABLE,
  output [31:0] WRITE_DATA
);

  wire ASel, BrEq, BrLt, BrUn, BSel, CSRSel, CSRWen, MemRW, PCSel, RegWEn;
  wire [1:0] WBsel;
  wire [2:0] ImmSel;
  wire [3:0] ALUSel;
  wire [31:0] adder_1_out, alu_1_result, demultiplexer_1_out0, demultiplexer_1_out2, demultiplexer_1_out3,
       imm_gen_1_imm, INSTRUCTION_EX, multiplexer_1_out, multiplexer_2_out, multiplexer_3_out,
       PROGRAM_COUNTER_EX, regfile_1_read_data_1, undriven, undriven_2;

  Multiplexer #(.enable("false"), .width(32)) multiplexer_1 (
    .in0(demultiplexer_1_out2), .in1(PROGRAM_COUNTER), .out(multiplexer_1_out), .sel(PCSel));
  Adder #(.width(32)) adder_1 (.a(multiplexer_1_out), .b(32'h4), .out(adder_1_out));  // open: cin, cout
  Register #(.width(32)) PC (.D(adder_1_out), .en(1'b1), .clk(clk), .Q(PROGRAM_COUNTER));  // open: clr
  Register #(.width(32)) register_1 (.D(PROGRAM_COUNTER), .en(1'b1), .clk(clk), .Q(PROGRAM_COUNTER_EX));  // open: clr
  Register #(.width(32)) register_2 (.D(INSTRUCTION), .en(1'b1), .clk(clk), .Q(INSTRUCTION_EX));  // open: clr
  control_logic control_logic_1 (
    .CSRWen(CSRWen), .PCSel(PCSel), .RegWEn(RegWEn), .ImmSel(ImmSel), .BrUn(BrUn), .ASel(ASel), .BSel(BSel),
    .ALUSel(ALUSel), .MemRW(MemRW), .WBSel(WBsel), .CSRSel(CSRSel), .inst(INSTRUCTION_EX), .BrEq(BrEq),
    .BrLt(BrLt));
  imm_gen imm_gen_1 (.inst(INSTRUCTION_EX), .ImmSel(ImmSel), .imm(imm_gen_1_imm));
  regfile regfile_1 (
    .rs1(INSTRUCTION_EX[19:15]), .rs2(INSTRUCTION_EX[24:20]), .rd(INSTRUCTION_EX[11:7]),
    .Write_Data(demultiplexer_1_out0), .RegWEn(RegWEn), .clk(clk), .ra(ra), .sp(sp), .t0(t0), .t1(t1),
    .t2(t2), .s0(s0), .s1(s1), .a0(a0), .Read_Data_1(regfile_1_read_data_1), .Read_Data_2(WRITE_DATA));
  branch_comp branch_comp_1 (.rs1(undriven_2), .rs2(undriven), .BrUn(BrUn), .BrEq(BrEq), .BrLt(BrLt));
  Multiplexer #(.enable("false"), .width(32)) multiplexer_2 (
    .in0(regfile_1_read_data_1), .in1(PROGRAM_COUNTER_EX), .out(multiplexer_2_out), .sel(ASel));
  Multiplexer #(.enable("false"), .width(32)) multiplexer_3 (
    .in0(WRITE_DATA), .in1(imm_gen_1_imm), .out(multiplexer_3_out), .sel(BSel));
  alu alu_1 (.Result(alu_1_result), .A(multiplexer_2_out), .B(multiplexer_3_out), .ALUSel(ALUSel));
  Demultiplexer #(.enable("false"), .select(2), .width(32)) demultiplexer_1 (
    .out0(demultiplexer_1_out0), .out1(WRITE_ADDRESS), .out2(demultiplexer_1_out2),
    .out3(demultiplexer_1_out3), .in(alu_1_result), .sel(WBsel));
  // csr csr_1: pin names not known; wires that end beside it: demultiplexer_1_out3, tohost

  // Notes on the sheet:
  //   Output to IMEM
  //   IMEM (do **NOT** move this)
  //   Inputs from IMEM
  //   It is OK to move the PC, RegFile, ALU, MEM, Branch Comp, Imm Gen, and Control Logic to wherever is most convenient for you when constructing your CPU, and to delete this text
  //   Inputs/Outputs for testing. Do **NOT** move these.
  //   Outputs To DMEM
  //   DMEM (do **NOT** move this)
  //   Inputs From DMEM
endmodule
