// Logisim project regfile.circ as structural Verilog: 1 circuit, main circuit regfile
module regfile (
  input  [4:0] rs1,
  input  [4:0] rs2,
  input  [4:0] rd,
  input  [31:0] Write_Data,
  input  RegWEn,
  input  clk,
  output [31:0] ra,
  output [31:0] sp,
  output [31:0] t0,
  output [31:0] t1,
  output [31:0] t2,
  output [31:0] s0,
  output [31:0] s1,
  output [31:0] a0,
  output [31:0] Read_Data_1,
  output [31:0] Read_Data_2
);

  wire demultiplexer_1_out1, demultiplexer_1_out2, demultiplexer_1_out3, demultiplexer_1_out4,
       demultiplexer_1_out5, demultiplexer_1_out6, demultiplexer_1_out7, demultiplexer_1_out8,
       demultiplexer_1_out9, demultiplexer_1_out10;
  wire [31:0] register_3_q, register_4_q;

  Demultiplexer #(.enable("false"), .select(5)) demultiplexer_1 (
    .out1(demultiplexer_1_out1), .out2(demultiplexer_1_out2), .out3(demultiplexer_1_out3),
    .out4(demultiplexer_1_out4), .out5(demultiplexer_1_out5), .out6(demultiplexer_1_out6),
    .out7(demultiplexer_1_out7), .out8(demultiplexer_1_out8), .out9(demultiplexer_1_out9),
    .out10(demultiplexer_1_out10), .in(RegWEn), .sel(rd));  // open: out0, out11, out12, out13, out14, out15, out16, out17, out18, out19, out20, out21, out22, out23, out24, out25, out26, out27, out28, out29, out30, out31
  Register #(.width(32)) register_1 (.D(Write_Data), .en(demultiplexer_1_out1), .clk(clk), .Q(ra));  // open: clr
  Register #(.width(32)) register_2 (.D(Write_Data), .en(demultiplexer_1_out2), .clk(clk), .Q(sp));  // open: clr
  Register #(.width(32)) register_3 (
    .D(Write_Data), .en(demultiplexer_1_out3), .clk(clk), .Q(register_3_q));  // open: clr
  Register #(.width(32)) register_4 (
    .D(Write_Data), .en(demultiplexer_1_out4), .clk(clk), .Q(register_4_q));  // open: clr
  Register #(.width(32)) register_5 (.D(Write_Data), .en(demultiplexer_1_out5), .clk(clk), .Q(t0));  // open: clr
  Register #(.width(32)) register_6 (.D(Write_Data), .en(demultiplexer_1_out6), .clk(clk), .Q(t1));  // open: clr
  Register #(.width(32)) register_7 (.D(Write_Data), .en(demultiplexer_1_out7), .clk(clk), .Q(t2));  // open: clr
  Register #(.width(32)) register_8 (.D(Write_Data), .en(demultiplexer_1_out8), .clk(clk), .Q(s0));  // open: clr
  Register #(.width(32)) register_9 (.D(Write_Data), .en(demultiplexer_1_out9), .clk(clk), .Q(s1));  // open: clr
  Register #(.width(32)) register_10 (.D(Write_Data), .en(demultiplexer_1_out10), .clk(clk), .Q(a0));  // open: clr
  Register #(.width(32)) register_11 (.D(Write_Data), .clk(clk));  // open: en, Q, clr
  Register #(.width(32)) register_12 (.D(Write_Data), .clk(clk));  // open: en, Q, clr
  Register #(.width(32)) register_13 (.D(Write_Data), .clk(clk));  // open: en, Q, clr
  Register #(.width(32)) register_14 (.D(Write_Data), .clk(clk));  // open: en, Q, clr
  Register #(.width(32)) register_15 (.D(Write_Data), .clk(clk));  // open: en, Q, clr
  Register #(.width(32)) register_16 (.D(Write_Data), .clk(clk));  // open: en, Q, clr
  Multiplexer #(.enable("false"), .select(5), .width(32)) multiplexer_1 (
    .in0({32{1'b0}}), .in1(ra), .in2(sp), .in3(register_3_q), .in4(register_4_q), .in5(t0), .in6(t1),
    .in7(t2), .in8(s0), .in9(s1), .in10(a0), .out(Read_Data_1), .sel(rs1));  // open: in11, in12, in13, in14, in15, in16, in17, in18, in19, in20, in21, in22, in23, in24, in25, in26, in27, in28, in29, in30, in31
  Multiplexer #(.enable("false"), .select(5), .width(32)) multiplexer_2 (
    .in0({32{1'b0}}), .in1(ra), .in2(sp), .in3(register_3_q), .in4(register_4_q), .in5(t0), .in6(t1),
    .in7(t2), .in8(s0), .in9(s1), .in10(a0), .out(Read_Data_2), .sel(rs2));  // open: in11, in12, in13, in14, in15, in16, in17, in18, in19, in20, in21, in22, in23, in24, in25, in26, in27, in28, in29, in30, in31

  // Other names for the same wires on the sheet: read_data1[31:0] = Read_Data_1; read_data2[31:0] = Read_Data_2;
  //   read_reg1[4:0] = rs1; read_reg2[4:0] = rs2; write_en = RegWEn; write_reg[4:0] = rd

  // Notes on the sheet:
  //   INPUTS to your circuit
  //   DON'T CHANGE THE LOCATIONS OF THE INPUTS AND OUTPUTS!
  //   These are DEBUG/TEST outputs from your circuit.
  //   OUTPUTS from your circuit
endmodule
